# Fritzing sketch v1 (saved by Fritzing 0.9.10b)

parts:
  Mod1 = Amica NodeMCU DEVKIT 1.0
  FC-1 = Sound Sensor
  J1 = Basic Servo

nets:
  N1: Mod1.pin1, Mod1.pin_10, FC-1.VCC
  N2: Mod1.pin2, Mod1.pin_25, FC-1.GND
  N3: Mod1.pin_15, J1.pulse
  N4: Mod1.pin_16, FC-1.OUT
